# Fritzing sketch miniController (saved by Fritzing 0.9.3b)
circuit board: 4cm x 5cm
breadboards: 1

parts:
  Part1 = Arduino Nano (Rev3.0)
  - = female pin header, 2 pins [form="♀ (female)"]
  switch = female pin header, 3 pins [form="♀ (female)"]
  Signal = female pin header, 2 pins [form="♀ (female)"]
  + = female pin header, 3 pins [form="♀ (female)"]
  GND = female pin header, 3 pins [form="♀ (female)"]
  s = female pin header, 3 pins [form="♀ (female)"]
  D5 = female pin header, 3 pins [form="♀ (female)"]

nets:
  N1: Part1.GND, -.pin2, switch.pin2, Signal.pin2, +.pin2, GND.pin2, s.pin2, D5.pin2
  N2: Part1.D2, +.pin1
  N3: Part1.D3, GND.pin1
  N4: Part1.D4, s.pin1
  N5: Part1.D5, D5.pin1
  N6: Part1.D10, Signal.pin1
  N7: Part1.VIN, -.pin1, +.pin3, GND.pin3, s.pin3, D5.pin3
  N8: Part1.A7, switch.pin1
  N9: Part1.A6, switch.pin3
